# Fritzing sketch Relay_4chanel_with_pumps (saved by Fritzing 0.9.3b)
breadboards: 1

parts:
  U1 = 4-Channel 5v Relay Shield [package=relay-4ch5v10a]
  Raspberry_Pi_1 = Raspberry Pi 3 [part_number=RPI-3-V1.2]
  M1 = RioRand LM2596
  M2 = DC Motor
  M3 = DC Motor

nets:
  VCC: U1.VCC, Raspberry_Pi_1.5V
  GND: U1.GND, Raspberry_Pi_1.GND
  N1: U1.IN1, Raspberry_Pi_1.GPIO18
  N2: U1.IN2, Raspberry_Pi_1.GPIO17
  N3: U1.K1-Off, M3.pin_1
  N4: U1.K1-On, U1.K2-On, M1.Pin_3
  N5: U1.K2-Off, M2.pin_1
  N6: U1.IN4, Raspberry_Pi_1.GPIO14
  N7: U1.IN3, Raspberry_Pi_1.GPIO15
  N8: M2.pin_2, M3.pin_2

notes:
  5v---------VCC
  GND ---------GND
  GPIO 14-----------IN4
  GPIO 15- ---------IN3
  GPIO 17---------IN2
  GPIO 18---------IN1
  Pump 1 ( add ph high)
  pin 17
  Pump 2 ( add ph low)
  pin 18
  AC Converter 220V to 12 V

custom parts:
  4-Channel 5v Relay Shield: 4 Channel 5v Relay Shield w. 2x SPD-06VDC-SD-C
  RioRand LM2596: Step-down DC-DC Converter (modified to correct all views by Peter Van Epp january 2018) Corrected the pins so the part works in all views. Changed the sizes in bb and pcb to match the data sheet. PCB view had a small outline (possibly only for wires), changed it to pads in the same places as the module and added holes in the PCB silkscreen layer where the mounting holes on the module are (you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
